# Fritzing sketch robotank_with_servo_and_sensor (saved by Fritzing 0.9.3b)
breadboards: 1

parts:
  ESP-12E_motorshield = ESP12E Motor Shield
  HC-SR04 = HC-SR04
  Amica_NodeMCU_(esp8266) = Amica NodeMCU DevKit 1.0
  S1 = Pushbutton [package="[SMD]"]
  S2 = Round Pushbutton
  SG-90 = Basic Servo
  battery_4_8v = 4 x AAA Battery Mount
  M1 = DC Motor
  M2 = DC Motor

nets:
  N1: ESP-12E_motorshield.D1, ESP-12E_motorshield.D5#7, ESP-12E_motorshield.D6#8, ESP-12E_motorshield.D7#9, ESP-12E_motorshield.D8#10, ESP-12E_motorshield.TX#12, ESP-12E_motorshield.3V3#14, HC-SR04.Trig, HC-SR04.Echo, S1.Pin_3, S1.Pin_4, SG-90.pulse
  N2: ESP-12E_motorshield.3V3#19, ESP-12E_motorshield.3V3#47, ESP-12E_motorshield.3V3#54, Amica_NodeMCU_(esp8266).pin1, Amica_NodeMCU_(esp8266).pin_10, Amica_NodeMCU_(esp8266).pin_26
  N3: ESP-12E_motorshield.G#33, ESP-12E_motorshield.G#44, ESP-12E_motorshield.G#48, ESP-12E_motorshield.G#55, Amica_NodeMCU_(esp8266).pin2, Amica_NodeMCU_(esp8266).pin_9, Amica_NodeMCU_(esp8266).pin_25, Amica_NodeMCU_(esp8266).pin_29
  N4: ESP-12E_motorshield.SD0, Amica_NodeMCU_(esp8266).pin_23
  N5: ESP-12E_motorshield.CMD, Amica_NodeMCU_(esp8266).pin_22
  N6: ESP-12E_motorshield.SD1, Amica_NodeMCU_(esp8266).pin_21
  N7: ESP-12E_motorshield.RSV#40, Amica_NodeMCU_(esp8266).pin_18
  N8: ESP-12E_motorshield.VIN#43, Amica_NodeMCU_(esp8266).pin_30
  N9: ESP-12E_motorshield.RST, Amica_NodeMCU_(esp8266).pin_28
  N10: ESP-12E_motorshield.EN, Amica_NodeMCU_(esp8266).pin_27
  N11: ESP-12E_motorshield.CLK, Amica_NodeMCU_(esp8266).pin_24
  N12: ESP-12E_motorshield.SD2, Amica_NodeMCU_(esp8266).pin_20
  N13: ESP-12E_motorshield.SD3, Amica_NodeMCU_(esp8266).pin_19
  N14: ESP-12E_motorshield.RSV#52, Amica_NodeMCU_(esp8266).pin_17
  N15: ESP-12E_motorshield.AD0, Amica_NodeMCU_(esp8266).pin_16
  N16: ESP-12E_motorshield.TX#56, Amica_NodeMCU_(esp8266).pin3
  N17: ESP-12E_motorshield.RX, Amica_NodeMCU_(esp8266).pin4
  N18: ESP-12E_motorshield.D8#58, Amica_NodeMCU_(esp8266).pin5
  N19: ESP-12E_motorshield.D7#59, Amica_NodeMCU_(esp8266).pin6
  N20: ESP-12E_motorshield.D6#60, Amica_NodeMCU_(esp8266).pin7
  N21: ESP-12E_motorshield.D5#61, Amica_NodeMCU_(esp8266).pin8
  N22: ESP-12E_motorshield.CB, Amica_NodeMCU_(esp8266).pin_11
  N23: ESP-12E_motorshield.DA, Amica_NodeMCU_(esp8266).pin_12
  N24: ESP-12E_motorshield.PWMB, Amica_NodeMCU_(esp8266).pin_13
  N25: ESP-12E_motorshield.PWMA, Amica_NodeMCU_(esp8266).pin_14
  N26: ESP-12E_motorshield.D0, Amica_NodeMCU_(esp8266).pin_15
  N27: ESP-12E_motorshield.VIN#74, ESP-12E_motorshield.VM
  N28: ESP-12E_motorshield.V#80, HC-SR04.Vcc
  N29: ESP-12E_motorshield.V#81, SG-90.vcc
  N30: ESP-12E_motorshield.G#88, S1.Pin_1, S1.Pin_2
  N31: ESP-12E_motorshield.G#90, HC-SR04.Gnd
  N32: ESP-12E_motorshield.G#91, SG-90.gnd
  N33: ESP-12E_motorshield.A-, M1.pin_1
  N34: ESP-12E_motorshield.A+, M1.pin_2
  N35: ESP-12E_motorshield.B-, M2.pin_1
  N36: ESP-12E_motorshield.B+, M2.pin_2
  N37: ESP-12E_motorshield.VIN#102, battery_4_8v.+
  N38: ESP-12E_motorshield.GND, S2.leg1
  N39: S2.leg0, battery_4_8v.-

custom parts:
  ESP12E Motor Shield: ESP8266 WiFi Motor Drive Expansion Board For NodeMCU ESP-12E
  HC-SR04: HC-SR04 ultrasonic distance sensor
  Amica NodeMCU DevKit 1.0: Amica NodeMCU DEVKIT 1.0 Development Kit based on ESP8266 ESP-12E, integating GPIO, PWM, IIC, 1-Wire and ADC all in one board.
